# Fritzing sketch DCC-Solenoid-Turnout-Driver (saved by Fritzing 0.9.3b)
circuit board: 8.5cm x 10cm
breadboards: 1

parts:
  1 = female pin header, 3 pins [form="♀ (female)"]
  2 = female pin header, 3 pins [form="♀ (female)"]
  3 = female pin header, 3 pins [form="♀ (female)"]
  4 = female pin header, 3 pins [form="♀ (female)"]
  5 = female pin header, 3 pins [form="♀ (female)"]
  6 = female pin header, 3 pins [form="♀ (female)"]
  7 = female pin header, 3 pins [form="♀ (female)"]
  ULN1 = Darlington Driver [package=dil18]
  ULN2 = Darlington Driver [package=dil18]
  8 = female pin header, 3 pins [form="♀ (female)"]
  J9 = double row female pin header, 20 pins [form="♀ (female)"]
  MCP23017 = female pin header, 10 pins [form="♀ (female)"]
  R1 = Resistor [tolerance=±5% resistance=470 power=0.25 package=THT]
  LED1 = LED - 5mm [color="Red (633nm)" current=0.030 package="5 mm [THT]"]
  J14 = male pin header, 2 pins [form="♂ (male)"]
  J12 = male pin header, 2 pins [form="♂ (male)"]
  J13 = male pin header, 2 pins [form="♂ (male)"]
  J11 = male pin header, 4 pins [form="♂ (male)"]
  J15 = male pin header, 4 pins [form="♂ (male)"]
  R2 = Resistor [tolerance=±5% resistance=10k power=0.25 package=THT]
  R3 = Resistor [tolerance=±5% resistance=10k power=0.25 package=THT]
  R4 = Resistor [tolerance=±5% resistance=10k power=0.25 package=THT]
  C1_+ = female pin header, 1 pin [form="♀ (female)"]
  C1_- = female pin header, 1 pin [form="♀ (female)"]
  J16 = female pin header, 2 pins [form="♀ (female)"]
  D1 = Zener Diode [part_number=1N4732A breakdown_voltage=3.6V package="300 mil [THT]"]
  -1 = female pin header, 2 pins [form="♀ (female)"]
  BR2 = female alternating pin header, 2 pins [form="♀ (female)"]
  R5 = Resistor [tolerance=±5% resistance=2.2k power=0.25 package=THT]
  R6 = Resistor [tolerance=±5% resistance=2.2k power=0.25 package=THT]
  R7 = Resistor [tolerance=±5% resistance=2.2k power=0.25 package=THT]
  Q2 = npn-Powertransistor [package="TO220 [THT]"]
  C3 = Electrolytic Capacitor [capacitance=470µF voltage=35V package="300 mil [THT, electrolytic]"]
  C2 = Electrolytic Capacitor [capacitance=470µF voltage=35V package="300 mil [THT, electrolytic]"]
  J18 = female pin header, 1 pin [form="♀ (female)"]
  LED2 = LED - 3mm [color="Red (633nm)" current=0.030 package="3 mm [THT]"]
  D2 = Rectifier Diode [part_number=1N4001 package="300 mil [THT]"]
  R8 = Resistor [tolerance=±5% resistance=1k power=0.25 package=THT]
  J8 = female pin header, 2 pins [form="♀ (female)"]
  J21 = double row female pin header, 20 pins [form="♀ (female)"]  # not connected
  J22 = double row female pin header, 20 pins [form="♀ (female)"]  # not connected
  J23 = double row female pin header, 20 pins [form="♀ (female)"]  # not connected
  J24 = double row female pin header, 20 pins [form="♀ (female)"]  # not connected
  J20 = double row female pin header, 16 pins [form="♀ (female)"]  # not connected
  J17 = screw terminal, 2 pins
  J19 = screw terminal, 2 pins

nets:
  N1: 1.pin1, 2.pin1, 3.pin1, 4.pin1, 5.pin1, 6.pin1, 7.pin1, ULN1.10, ULN2.10, 8.pin1, C1_+.pin1, D2.cathode, R8.Pin_1, J8.pin1, J19.pin1
  N2: 1.pin2, ULN1.18
  N3: 1.pin3, ULN1.17
  N4: 2.pin2, ULN1.16
  N5: 2.pin3, ULN1.15
  N6: 3.pin2, ULN1.14
  N7: 3.pin3, ULN1.13
  N8: 4.pin2, ULN1.12
  N9: 4.pin3, ULN1.11
  N10: 5.pin2, ULN2.18
  N11: 5.pin3, ULN2.17
  N12: 6.pin2, ULN2.16
  N13: 6.pin3, ULN2.15
  N14: 7.pin2, ULN2.14
  N15: 7.pin3, ULN2.13
  N16: ULN1.1, J9.pin20
  N17: ULN1.2, J9.pin19
  N18: ULN1.3, J9.pin18
  N19: ULN1.4, J9.pin17
  N20: ULN1.5, J9.pin16
  N21: ULN1.6, J9.pin15
  N22: ULN1.7, J9.pin14
  N23: ULN1.8, J9.pin13
  N24: ULN1.9, ULN2.9, J9.pin11, C1_-.pin1, J16.pin1, J16.pin2, D1.anode, -1.pin1, C3.-, C2.-, LED2.cathode, J8.pin2, J19.pin2
  N25: ULN2.1, J9.pin1
  N26: ULN2.2, J9.pin2
  N27: ULN2.3, J9.pin3
  N28: ULN2.4, J9.pin4
  N29: ULN2.5, J9.pin5
  N30: ULN2.6, J9.pin6
  N31: ULN2.7, J9.pin7
  N32: ULN2.8, J9.pin8
  N33: ULN2.11, 8.pin3
  N34: ULN2.12, 8.pin2
  N35: MCP23017.pin1, R1.Pin_0, J14.pin1, J12.pin1, J13.pin1, J11.pin1, J15.pin1
  N36: MCP23017.pin2, LED1.cathode, J11.pin2, J15.pin2, R2.Pin_0, R3.Pin_0, R4.Pin_0
  N37: MCP23017.pin3, J11.pin4, J15.pin4
  N38: MCP23017.pin4, J11.pin3, J15.pin3
  N39: MCP23017.pin8, J14.pin2, R2.Pin_1
  N40: MCP23017.pin9, J13.pin2, R3.Pin_1
  N41: MCP23017.pin10, J12.pin2, R4.Pin_1
  N42: R1.Pin_1, LED1.anode
  N43: D1.cathode, Q2.emitter, C3.+, C2.+, J18.pin1, D2.anode
  N44: -1.pin2, J17.pin2
  N45: BR2.pin1, J17.pin1
  N46: BR2.pin2, R5.Pin_1, R6.Pin_1, R7.Pin_1, Q2.collector
  N47: R5.Pin_0, R6.Pin_0, R7.Pin_0, Q2.base
  N48: LED2.anode, R8.Pin_0

notes:
  VCC
  GND
  SCL
  SDA
  A0
  A1
  A2
  A3
  A4
  A5
  A6
  A7
  B0
  B1
  B2
  B3
  B4
  B6
  B5
  B7
  0
  1
  2
  +
  -
  C
  Input
  Output
  4x4CDUP4
  I2C
  B
  E
